// Logisim project d_flipflop.circ as structural Verilog
module main (
  input  D,
  input  CLK,
  output Q,
  output NQ,
  output Q_vhd1,
  output NQ_vhd1
);

  wire master_q, not_1_out;

  not not_1 (not_1_out, CLK);
  dlatch_gate master (.D(D), .EN(not_1_out), .Q(master_q));  // open: NQ
  d_flipflop d_flipflop_1 (.clk(CLK), .d(D), .q(Q_vhd1), .nq(NQ_vhd1));
  dlatch_gate slave (.D(master_q), .EN(CLK), .Q(Q), .NQ(NQ));
endmodule

module dlatch_gate (
  input  D,
  input  EN,
  output Q,
  output NQ
);

  wire nand_1_out, nand_2_out, not_1_out;

  not not_1 (not_1_out, D);
  nand nand_1 (nand_1_out, D, EN);
  nand nand_2 (nand_2_out, not_1_out, EN);
  nand nand_3 (Q, nand_1_out, NQ);
  nand nand_4 (NQ, nand_2_out, Q);

  // Notes on the sheet:
  //   EN: initial=0x1
endmodule

// VHDL entity d_latch, as the project stores it:
LIBRARY ieee;
USE ieee.std_logic_1164.ALL;

ENTITY d_latch IS
  PORT (
    en : IN  std_logic;
    d  : IN  std_logic;
    q  : OUT std_logic;
    nq : OUT std_logic
  );
END d_latch;

ARCHITECTURE bhv OF d_latch IS
  SIGNAL q_int : std_logic := '0';
BEGIN
  PROCESS(en, d)
  BEGIN
    IF (en = '1') THEN
      q_int <= d;
    END IF;
  END PROCESS;

  q  <= q_int;
  nq <= NOT q_int;
END bhv;

// VHDL entity d_flipflop, as the project stores it:
LIBRARY ieee;
USE ieee.std_logic_1164.ALL;

ENTITY d_flipflop IS
  PORT (
    clk : IN  std_logic;
    d   : IN  std_logic;
    q   : OUT std_logic;
    nq  : OUT std_logic
  );
END d_flipflop;

ARCHITECTURE bhv OF d_flipflop IS
  SIGNAL q_int : std_logic := '0';
BEGIN
  PROCESS(clk)
  BEGIN
    IF rising_edge(clk) THEN
      q_int <= d;
    END IF;
  END PROCESS;

  q  <= q_int;
  nq <= NOT q_int;
END bhv;
