// Logisim project d_latch.circ as structural Verilog
module main (
  input  D,
  input  EN,
  output Q,
  output NQ,
  output Q_vhd1,
  output NQ_vhd1
);

  wire nand_1_out, nand_2_out, not_1_out;

  not not_1 (not_1_out, D);
  nand nand_1 (nand_1_out, D, EN);
  nand nand_2 (nand_2_out, not_1_out, EN);
  nand nand_3 (Q, nand_1_out, NQ);
  nand nand_4 (NQ, nand_2_out, Q);
  d_latch d_latch_1 (.en(EN), .d(D), .q(Q_vhd1), .nq(NQ_vhd1));

  // Notes on the sheet:
  //   EN: initial=0x1
endmodule

// VHDL entity d_latch, as the project stores it:
LIBRARY ieee;
USE ieee.std_logic_1164.ALL;

ENTITY d_latch IS
  PORT (
    en : IN  std_logic;
    d  : IN  std_logic;
    q  : OUT std_logic;
    nq : OUT std_logic
  );
END d_latch;

ARCHITECTURE bhv OF d_latch IS
  SIGNAL q_int : std_logic := '0';
BEGIN
  PROCESS(en, d)
  BEGIN
    IF (en = '1') THEN
      q_int <= d;
    END IF;
  END PROCESS;

  q  <= q_int;
  nq <= NOT q_int;
END bhv;
