// Logisim project dff_async_sc.circ as structural Verilog
module main (
  input  SET,
  input  CLK,
  input  D,
  input  CLR,
  output Q,
  output NQ,
  output Q_vhdl,
  output NQ_vhdl
);

  wire nand_1_out, nand_2_out, nand_3_out, nand_4_out, nand_5_out, not_1_out;

  not not_1 (not_1_out, CLR);
  nand nand_1 (nand_1_out, SET, not_1_out);
  nand nand_2 (nand_2_out, nand_1_out, nand_5_out, nand_3_out);
  nand nand_3 (nand_3_out, nand_2_out, not_1_out, CLK);
  nand nand_4 (nand_4_out, nand_3_out, CLK, nand_5_out);
  nand nand_5 (nand_5_out, nand_4_out, not_1_out, D);
  dff_async_sc dff_async_sc_1 (.clk(CLK), .d(D), .set(SET), .clr(CLR), .q(Q_vhdl), .nq(NQ_vhdl));
  nand nand_6 (Q, nand_1_out, nand_3_out, NQ);
  nand nand_7 (NQ, Q, nand_4_out, not_1_out);

  // Notes on the sheet:
  //   CLR: initial=0x1
endmodule

// VHDL entity dff_async_sc, as the project stores it:
LIBRARY ieee;
USE ieee.std_logic_1164.ALL;

ENTITY dff_async_sc IS
  PORT (
    clk : IN  std_logic;
    d   : IN  std_logic;
    set : IN  std_logic;
    clr : IN  std_logic;
    q   : OUT std_logic;
    nq  : OUT std_logic
  );
END dff_async_sc;

ARCHITECTURE bhv OF dff_async_sc IS
  SIGNAL q_int : std_logic := '0';
BEGIN
  PROCESS(clk, clr, set)
  BEGIN
    IF (clr = '1') THEN
      q_int <= '0';
    ELSIF (set = '1') THEN
      q_int <= '1';
    ELSIF rising_edge(clk) THEN
      q_int <= d;
    END IF;
  END PROCESS;

  q  <= q_int;
  nq <= NOT q_int;
END bhv;
