// Logisim project jk_flipflop.circ as structural Verilog
module main (
  input  J,
  input  CLK,
  input  K,
  input  CLR,
  output Q,
  output NQ,
  output Q_vhd1,
  output NQ_vhd1
);

  wire nand_1_out, nand_2_out, nand_3_out, nand_4_out, nand_5_out, nand_6_out, not_1_out, not_2_out;

  not not_1 (not_1_out, CLR);
  not not_2 (not_2_out, CLK);
  nand nand_1 (nand_1_out, J, not_2_out, NQ);
  nand nand_2 (nand_2_out, K, not_2_out, Q);
  nand nand_3 (nand_3_out, nand_1_out, nand_4_out);
  nand nand_4 (nand_4_out, nand_3_out, nand_2_out, not_1_out);
  jk_flipflop jk_flipflop_1 (.clk(CLK), .clr(CLR), .j(J), .k(K), .q(Q_vhd1), .nq(NQ_vhd1));
  nand nand_5 (nand_5_out, nand_3_out, CLK);
  nand nand_6 (nand_6_out, CLK, nand_4_out);
  nand nand_7 (Q, nand_5_out, NQ);
  nand nand_8 (NQ, Q, nand_6_out, not_1_out);

  // Notes on the sheet:
  //   CLR: initial=0x1
endmodule

// VHDL entity jk_flipflop, as the project stores it:
LIBRARY ieee;
USE ieee.std_logic_1164.ALL;

ENTITY jk_flipflop IS
  PORT (
    clk : IN  std_logic;
    clr : IN  std_logic;
    j   : IN  std_logic;
    k   : IN  std_logic;
    q   : OUT std_logic;
    nq  : OUT std_logic
  );
END jk_flipflop;

ARCHITECTURE bhv OF jk_flipflop IS
  SIGNAL q_internal : std_logic := '0';
BEGIN
  PROCESS(clk, clr)
  BEGIN
    IF (clr = '1') THEN
      q_internal <= '0';
    ELSIF rising_edge(clk) THEN
      IF (j = '0' AND k = '0') THEN
        q_internal <= q_internal;
      ELSIF (j = '0' AND k = '1') THEN
        q_internal <= '0';
      ELSIF (j = '1' AND k = '0') THEN
        q_internal <= '1';
      ELSIF (j = '1' AND k = '1') THEN
        q_internal <= NOT q_internal;
      END IF;
    END IF;
  END PROCESS;

  q  <= q_internal;
  nq <= NOT q_internal;
END bhv;
