// Logisim project rs_latch.circ as structural Verilog
module main (
  input  R,
  input  S,
  output Q,
  output NQ,
  output Q_vhd1,
  output NQ_vhd1
);

  nor nor_1 (Q, R, NQ);
  nor nor_2 (NQ, Q, S);
  rs_latch rs_latch_1 (.s(S), .r(R), .q(Q_vhd1), .nq(NQ_vhd1));

  // Notes on the sheet:
  //   R: initial=0x1
endmodule

// VHDL entity rs_latch, as the project stores it:
LIBRARY ieee;
USE ieee.std_logic_1164.ALL;

ENTITY rs_latch IS
  PORT (
    s  : IN  std_logic;
    r  : IN  std_logic;
    q  : OUT std_logic;
    nq : OUT std_logic
  );
END rs_latch;

ARCHITECTURE bhv OF rs_latch IS
  SIGNAL q_int  : std_logic := '0';
  SIGNAL nq_int : std_logic := '1';
BEGIN
  q_int  <= r NOR nq_int;
  nq_int <= s NOR q_int;
  q  <= q_int;
  nq <= nq_int;
END bhv;
